// Logisim project CPU.circ as structural Verilog: 24 circuits, main circuit CPU
module CPU (
);

  wire clock_1_out, controller_1_alu_enable_if_it_is_an_arithmetic_operation, controller_1_instructionread,
       controller_1_jump, controller_1_jump_mux_select, controller_1_load_memread,
       controller_1_mux1_imm_or_register, controller_1_rd2_select_registerfile, controller_1_store_memwrite,
       controller_1_wr_select_registerfile, controller_1_writeenable_alu_mem;
  wire [2:0] compare20_1_out_3;
  wire [3:0] controller_1_dest_op1_srcst, controller_1_src1_op2, controller_1_src2, multiplexer_2_out;
  wire [11:0] multiplexer_1_out, pc_1_output, ram_1_data, signextender8to12_1_out;
  wire [19:0] alu_1_output, multiplexer_3_out, multiplexer_4_out, ram_2_data, registerfile_1_outputdata1,
       registerfile_1_outputdata2, signextender7to20_1_out;
  wire [19:12] ram_1_data_2;

  Clock clock_1 (.out(clock_1_out));
  Multiplexer #(.width(12), .enable("false")) multiplexer_1 (
    .in0(signextender8to12_1_out), .in1(ram_1_data), .out(multiplexer_1_out),
    .sel(controller_1_jump_mux_select));
  PC pc_1 (.\input (multiplexer_1_out), .\output (pc_1_output), .JUMP(controller_1_jump), .clock(clock_1_out));
  SignExtender8to12 signextender8to12_1 (.In(ram_1_data[7:0]), .OUT(signextender8to12_1_out));
  RAM #(.addrWidth(12), .dataWidth(20)) ram_1 (
    .addr(pc_1_output), .data({ram_1_data_2, ram_1_data}), .sel(1'b1), .ld(controller_1_instructionread));  // open: clk, clr
  Multiplexer #(.width(4), .enable("false")) multiplexer_2 (
    .in0(controller_1_src2), .in1(controller_1_dest_op1_srcst), .out(multiplexer_2_out),
    .sel(controller_1_rd2_select_registerfile));
  RegisterFile registerfile_1 (
    .rd1(controller_1_src1_op2), .WR(controller_1_dest_op1_srcst), .rd2(multiplexer_2_out),
    .outputData1(registerfile_1_outputdata1), .outputData2(registerfile_1_outputdata2),
    .WE(controller_1_writeenable_alu_mem), .inputData(multiplexer_4_out), .Clock(clock_1_out));
  Multiplexer #(.width(20), .enable("false")) multiplexer_3 (
    .in0(registerfile_1_outputdata2), .in1(signextender7to20_1_out), .out(multiplexer_3_out),
    .sel(controller_1_mux1_imm_or_register));
  SignExtender7to20 signextender7to20_1 (.In({ram_1_data_2, ram_1_data}), .OUT(signextender7to20_1_out));
  ALU alu_1 (
    .i0(registerfile_1_outputdata1), .i1(multiplexer_3_out), .\output (alu_1_output),
    .enable(controller_1_alu_enable_if_it_is_an_arithmetic_operation),
    .opcode_ALU_control(ram_1_data_2[19:16]));
  Compare20 compare20_1 (.A(registerfile_1_outputdata2), .B(registerfile_1_outputdata1), .out_3(compare20_1_out_3));
  Multiplexer #(.width(20), .enable("false")) multiplexer_4 (
    .in0(alu_1_output), .in1(ram_2_data), .out(multiplexer_4_out), .sel(controller_1_wr_select_registerfile));
  Controller controller_1 (
    .src2(controller_1_src2), .src1_op2(controller_1_src1_op2), .dest_op1_srcST(controller_1_dest_op1_srcst),
    .\input ({ram_1_data_2, ram_1_data}), .Mux1_imm_or_register(controller_1_mux1_imm_or_register),
    .ALU_enable_if_it_is_an_arithmetic_operation(controller_1_alu_enable_if_it_is_an_arithmetic_operation),
    .wr_select_registerfile(controller_1_wr_select_registerfile),
    .InstructionRead(controller_1_instructionread), .load_MemRead(controller_1_load_memread),
    .store_MemWrite(controller_1_store_memwrite), .BCMP_bits(compare20_1_out_3), .JUMP(controller_1_jump),
    .JUMP_MUX_SELECT(controller_1_jump_mux_select),
    .rd2_select_registerfile(controller_1_rd2_select_registerfile),
    .WriteEnable_ALU_MEM(controller_1_writeenable_alu_mem));  // open: PCRead, BCMP_ENABLE
  RAM #(.addrWidth(12), .dataWidth(20), .bus("separate")) ram_2 (
    .addr(ram_1_data), .din(registerfile_1_outputdata2), .data(ram_2_data),
    .str(controller_1_store_memwrite), .sel(1'b1), .clk(clock_1_out), .ld(controller_1_load_memread),
    .clr(1'b0));

  // Notes on the sheet:
  //   Instruction Memory
  //   CPU
  //   Mux1: Imm or register
  //   opcode
  //   mux2
  //   Data Memory
endmodule

module FullAdder (
  input  i0,
  input  i1,
  input  cin,
  output sum,
  output cout
);

  wire and_1_out, and_2_out, and_3_out, xor_1_out;

  xor xor_1 (xor_1_out, i0, i1);
  xor xor_2 (sum, xor_1_out, cin);
  and and_1 (and_1_out, i0, i1);
  and and_2 (and_2_out, i1, cin);
  and and_3 (and_3_out, i0, cin);
  or or_1 (cout, and_1_out, and_2_out, and_3_out);

  // Notes on the sheet:
  //   FULLADDER
endmodule

module Adder20 (
  input  [19:0] num0,
  input  [19:0] num1,
  output [19:0] sum
);

  wire fulladder_2_cout, fulladder_3_cout, fulladder_4_cout, fulladder_5_cout, fulladder_6_cout,
       fulladder_7_cout, fulladder_8_cout, fulladder_9_cout, fulladder_10_cout, fulladder_11_cout,
       fulladder_12_cout, fulladder_13_cout, fulladder_14_cout, fulladder_15_cout, fulladder_16_cout,
       fulladder_17_cout, fulladder_18_cout, fulladder_19_cout, fulladder_20_cout;

  FullAdder fulladder_1 (.i0(num0[19]), .i1(num1[19]), .cin(fulladder_2_cout), .sum(sum[19]));  // open: cout
  FullAdder fulladder_2 (.i0(num0[18]), .i1(num1[18]), .cin(fulladder_3_cout), .sum(sum[18]), .cout(fulladder_2_cout));
  FullAdder fulladder_3 (.i0(num0[17]), .i1(num1[17]), .cin(fulladder_4_cout), .sum(sum[17]), .cout(fulladder_3_cout));
  FullAdder fulladder_4 (.i0(num0[16]), .i1(num1[16]), .cin(fulladder_5_cout), .sum(sum[16]), .cout(fulladder_4_cout));
  FullAdder fulladder_5 (.i0(num0[15]), .i1(num1[15]), .cin(fulladder_6_cout), .sum(sum[15]), .cout(fulladder_5_cout));
  FullAdder fulladder_6 (.i0(num0[14]), .i1(num1[14]), .cin(fulladder_7_cout), .sum(sum[14]), .cout(fulladder_6_cout));
  FullAdder fulladder_7 (.i0(num0[13]), .i1(num1[13]), .cin(fulladder_8_cout), .sum(sum[13]), .cout(fulladder_7_cout));
  FullAdder fulladder_8 (.i0(num0[12]), .i1(num1[12]), .cin(fulladder_10_cout), .sum(sum[12]), .cout(fulladder_8_cout));
  FullAdder fulladder_9 (.i0(num0[10]), .i1(num1[10]), .cin(fulladder_11_cout), .sum(sum[10]), .cout(fulladder_9_cout));
  FullAdder fulladder_10 (
    .i0(num0[11]), .i1(num1[11]), .cin(fulladder_9_cout), .sum(sum[11]), .cout(fulladder_10_cout));
  FullAdder fulladder_11 (.i0(num0[9]), .i1(num1[9]), .cin(fulladder_12_cout), .sum(sum[9]), .cout(fulladder_11_cout));
  FullAdder fulladder_12 (.i0(num0[8]), .i1(num1[8]), .cin(fulladder_13_cout), .sum(sum[8]), .cout(fulladder_12_cout));
  FullAdder fulladder_13 (.i0(num0[7]), .i1(num1[7]), .cin(fulladder_14_cout), .sum(sum[7]), .cout(fulladder_13_cout));
  FullAdder fulladder_14 (.i0(num0[6]), .i1(num1[6]), .cin(fulladder_15_cout), .sum(sum[6]), .cout(fulladder_14_cout));
  FullAdder fulladder_15 (.i0(num0[5]), .i1(num1[5]), .cin(fulladder_16_cout), .sum(sum[5]), .cout(fulladder_15_cout));
  FullAdder fulladder_16 (.i0(num0[4]), .i1(num1[4]), .cin(fulladder_18_cout), .sum(sum[4]), .cout(fulladder_16_cout));
  FullAdder fulladder_17 (.i0(num0[2]), .i1(num1[2]), .cin(fulladder_19_cout), .sum(sum[2]), .cout(fulladder_17_cout));
  FullAdder fulladder_18 (.i0(num0[3]), .i1(num1[3]), .cin(fulladder_17_cout), .sum(sum[3]), .cout(fulladder_18_cout));
  FullAdder fulladder_19 (.i0(num0[1]), .i1(num1[1]), .cin(fulladder_20_cout), .sum(sum[1]), .cout(fulladder_19_cout));
  FullAdder fulladder_20 (.i0(num0[0]), .i1(num1[0]), .cin(1'b0), .sum(sum[0]), .cout(fulladder_20_cout));

  // Notes on the sheet:
  //   20 BITS ADDER
endmodule

module DFlipFLop (
  input  D,
  input  clk,
  output Q
);

  wire dlatch_1_q, not_1_out;

  DLatch dlatch_1 (.D(D), .clk(clk), .Q(dlatch_1_q));  // open: Q_prime
  not not_1 (not_1_out, clk);
  DLatch dlatch_2 (.D(dlatch_1_q), .clk(not_1_out), .Q(Q));  // open: Q_prime

  // Notes on the sheet:
  //   didi not use it
endmodule

module RegisterFile (
  input  [3:0] rd2,
  input  [3:0] rd1,
  input  [3:0] WR,
  input  Clock,
  input  WE,
  input  [19:0] inputData,
  output [19:0] outputData1,
  output [19:0] outputData2
);

  wire and_1_out, and_2_out, and_3_out, and_4_out, and_5_out, and_6_out, and_7_out, and_8_out, and_9_out,
       and_10_out, and_11_out, and_12_out, and_13_out, and_14_out, and_15_out, and_16_out, decoder16_1__0,
       decoder16_1__1, decoder16_1__2, decoder16_1__3, decoder16_1__4, decoder16_1__5, decoder16_1__6,
       decoder16_1__7, decoder16_1__8, decoder16_1__9, decoder16_1__10, decoder16_1__11, decoder16_1__12,
       decoder16_1__13, decoder16_1__14, decoder16_1__15, decoder16_2__0, decoder16_2__1, decoder16_2__2,
       decoder16_2__3, decoder16_2__4, decoder16_2__5, decoder16_2__6, decoder16_2__7, decoder16_2__8,
       decoder16_2__9, decoder16_2__10, decoder16_2__11, decoder16_2__12, decoder16_2__13, decoder16_2__14,
       decoder16_2__15, decoder16_3__0, decoder16_3__1, decoder16_3__2, decoder16_3__3, decoder16_3__4,
       decoder16_3__5, decoder16_3__6, decoder16_3__7, decoder16_3__8, decoder16_3__9, decoder16_3__10,
       decoder16_3__11, decoder16_3__12, decoder16_3__13, decoder16_3__14, decoder16_3__15;
  wire [19:0] register20_1_output, register20_2_output, register20_3_output, register20_4_output,
       register20_5_output, register20_6_output, register20_7_output, register20_8_output,
       register20_9_output, register20_10_output, register20_11_output, register20_12_output,
       register20_13_output, register20_14_output, register20_15_output, register20_16_output;

  Decoder16 decoder16_1 (
    ._0(decoder16_1__0), ._1(decoder16_1__1), ._2(decoder16_1__2), ._3(decoder16_1__3), ._4(decoder16_1__4),
    ._5(decoder16_1__5), ._6(decoder16_1__6), ._7(decoder16_1__7), ._8(decoder16_1__8), ._9(decoder16_1__9),
    ._10(decoder16_1__10), ._11(decoder16_1__11), ._12(decoder16_1__12), ._13(decoder16_1__13),
    ._14(decoder16_1__14), ._15(decoder16_1__15), .\input (rd1));
  Decoder16 decoder16_2 (
    ._0(decoder16_2__0), ._1(decoder16_2__1), ._2(decoder16_2__2), ._3(decoder16_2__3), ._4(decoder16_2__4),
    ._5(decoder16_2__5), ._6(decoder16_2__6), ._7(decoder16_2__7), ._8(decoder16_2__8), ._9(decoder16_2__9),
    ._10(decoder16_2__10), ._11(decoder16_2__11), ._12(decoder16_2__12), ._13(decoder16_2__13),
    ._14(decoder16_2__14), ._15(decoder16_2__15), .\input (WR));
  and and_1 (and_1_out, decoder16_2__0, WE);
  and and_2 (and_2_out, decoder16_2__1, WE);
  and and_3 (and_3_out, decoder16_2__2, WE);
  and and_4 (and_4_out, decoder16_2__3, WE);
  and and_5 (and_5_out, decoder16_2__4, WE);
  and and_6 (and_6_out, decoder16_2__5, WE);
  and and_7 (and_7_out, decoder16_2__6, WE);
  and and_8 (and_8_out, decoder16_2__7, WE);
  and and_9 (and_9_out, decoder16_2__8, WE);
  and and_10 (and_10_out, decoder16_2__9, WE);
  and and_11 (and_11_out, decoder16_2__10, WE);
  and and_12 (and_12_out, decoder16_2__11, WE);
  and and_13 (and_13_out, decoder16_2__12, WE);
  and and_14 (and_14_out, decoder16_2__13, WE);
  and and_15 (and_15_out, decoder16_2__14, WE);
  and and_16 (and_16_out, decoder16_2__15, WE);
  Register20 register20_1 (
    .\input (inputData), .clock(Clock), .clear(1'b0), .enable(and_1_out), .\output (register20_1_output));
  Register20 register20_2 (
    .\input (inputData), .clock(Clock), .clear(1'b0), .enable(and_2_out), .\output (register20_2_output));
  Register20 register20_3 (
    .\input (inputData), .clock(Clock), .clear(1'b0), .enable(and_3_out), .\output (register20_3_output));
  Register20 register20_4 (
    .\input (inputData), .clock(Clock), .clear(1'b0), .enable(and_4_out), .\output (register20_4_output));
  Register20 register20_5 (
    .\input (inputData), .clock(Clock), .clear(1'b0), .enable(and_5_out), .\output (register20_5_output));
  Register20 register20_6 (
    .\input (inputData), .clock(Clock), .clear(1'b0), .enable(and_6_out), .\output (register20_6_output));
  Register20 register20_7 (
    .\input (inputData), .clock(Clock), .clear(1'b0), .enable(and_7_out), .\output (register20_7_output));
  Register20 register20_8 (
    .\input (inputData), .clock(Clock), .clear(1'b0), .enable(and_8_out), .\output (register20_8_output));
  Register20 register20_9 (
    .\input (inputData), .clock(Clock), .clear(1'b0), .enable(and_9_out), .\output (register20_9_output));
  Register20 register20_10 (
    .\input (inputData), .clock(Clock), .clear(1'b0), .enable(and_10_out), .\output (register20_10_output));
  Register20 register20_11 (
    .\input (inputData), .clock(Clock), .clear(1'b0), .enable(and_11_out), .\output (register20_11_output));
  Register20 register20_12 (
    .\input (inputData), .clock(Clock), .clear(1'b0), .enable(and_12_out), .\output (register20_12_output));
  Register20 register20_13 (
    .\input (inputData), .clock(Clock), .clear(1'b0), .enable(and_13_out), .\output (register20_13_output));
  Register20 register20_14 (
    .\input (inputData), .clock(Clock), .clear(1'b0), .enable(and_14_out), .\output (register20_14_output));
  Register20 register20_15 (
    .\input (inputData), .clock(Clock), .clear(1'b0), .enable(and_15_out), .\output (register20_15_output));
  Register20 register20_16 (
    .\input (inputData), .clock(Clock), .clear(1'b0), .enable(and_16_out), .\output (register20_16_output));
  assign outputData2 = decoder16_3__0 ? register20_1_output : 20'bz;  // Controlled_Buffer controlled_buffer_1
  assign outputData1 = decoder16_1__0 ? register20_1_output : 20'bz;  // Controlled_Buffer controlled_buffer_2
  assign outputData2 = decoder16_3__1 ? register20_2_output : 20'bz;  // Controlled_Buffer controlled_buffer_3
  assign outputData1 = decoder16_1__1 ? register20_2_output : 20'bz;  // Controlled_Buffer controlled_buffer_4
  assign outputData2 = decoder16_3__2 ? register20_3_output : 20'bz;  // Controlled_Buffer controlled_buffer_5
  assign outputData1 = decoder16_1__2 ? register20_3_output : 20'bz;  // Controlled_Buffer controlled_buffer_6
  assign outputData2 = decoder16_3__3 ? register20_4_output : 20'bz;  // Controlled_Buffer controlled_buffer_7
  assign outputData1 = decoder16_1__3 ? register20_4_output : 20'bz;  // Controlled_Buffer controlled_buffer_8
  assign outputData2 = decoder16_3__4 ? register20_5_output : 20'bz;  // Controlled_Buffer controlled_buffer_9
  assign outputData1 = decoder16_1__4 ? register20_5_output : 20'bz;  // Controlled_Buffer controlled_buffer_10
  assign outputData2 = decoder16_3__5 ? register20_6_output : 20'bz;  // Controlled_Buffer controlled_buffer_11
  assign outputData1 = decoder16_1__5 ? register20_6_output : 20'bz;  // Controlled_Buffer controlled_buffer_12
  assign outputData2 = decoder16_3__6 ? register20_7_output : 20'bz;  // Controlled_Buffer controlled_buffer_13
  assign outputData1 = decoder16_1__6 ? register20_7_output : 20'bz;  // Controlled_Buffer controlled_buffer_14
  assign outputData2 = decoder16_3__7 ? register20_8_output : 20'bz;  // Controlled_Buffer controlled_buffer_15
  assign outputData1 = decoder16_1__7 ? register20_8_output : 20'bz;  // Controlled_Buffer controlled_buffer_16
  assign outputData2 = decoder16_3__8 ? register20_9_output : 20'bz;  // Controlled_Buffer controlled_buffer_17
  assign outputData1 = decoder16_1__8 ? register20_9_output : 20'bz;  // Controlled_Buffer controlled_buffer_18
  assign outputData2 = decoder16_3__9 ? register20_10_output : 20'bz;  // Controlled_Buffer controlled_buffer_19
  assign outputData1 = decoder16_1__9 ? register20_10_output : 20'bz;  // Controlled_Buffer controlled_buffer_20
  assign outputData2 = decoder16_3__10 ? register20_11_output : 20'bz;  // Controlled_Buffer controlled_buffer_21
  assign outputData1 = decoder16_1__10 ? register20_11_output : 20'bz;  // Controlled_Buffer controlled_buffer_22
  assign outputData2 = decoder16_3__11 ? register20_12_output : 20'bz;  // Controlled_Buffer controlled_buffer_23
  assign outputData1 = decoder16_1__11 ? register20_12_output : 20'bz;  // Controlled_Buffer controlled_buffer_24
  assign outputData2 = decoder16_3__12 ? register20_13_output : 20'bz;  // Controlled_Buffer controlled_buffer_25
  assign outputData1 = decoder16_1__12 ? register20_13_output : 20'bz;  // Controlled_Buffer controlled_buffer_26
  assign outputData2 = decoder16_3__13 ? register20_14_output : 20'bz;  // Controlled_Buffer controlled_buffer_27
  assign outputData1 = decoder16_1__13 ? register20_14_output : 20'bz;  // Controlled_Buffer controlled_buffer_28
  assign outputData2 = decoder16_3__14 ? register20_15_output : 20'bz;  // Controlled_Buffer controlled_buffer_29
  assign outputData1 = decoder16_1__14 ? register20_15_output : 20'bz;  // Controlled_Buffer controlled_buffer_30
  assign outputData2 = decoder16_3__15 ? register20_16_output : 20'bz;  // Controlled_Buffer controlled_buffer_31
  assign outputData1 = decoder16_1__15 ? register20_16_output : 20'bz;  // Controlled_Buffer controlled_buffer_32
  Decoder16 decoder16_3 (
    ._0(decoder16_3__0), ._1(decoder16_3__1), ._2(decoder16_3__2), ._3(decoder16_3__3), ._4(decoder16_3__4),
    ._5(decoder16_3__5), ._6(decoder16_3__6), ._7(decoder16_3__7), ._8(decoder16_3__8), ._9(decoder16_3__9),
    ._10(decoder16_3__10), ._11(decoder16_3__11), ._12(decoder16_3__12), ._13(decoder16_3__13),
    ._14(decoder16_3__14), ._15(decoder16_3__15), .\input (rd2));

  // Notes on the sheet:
  //   20 BIT REGISTER FILE
endmodule

module Decoder16 (
  input  [3:0] \input ,
  output _0,
  output _1,
  output _2,
  output _3,
  output _4,
  output _5,
  output _6,
  output _7,
  output _8,
  output _9,
  output _10,
  output _11,
  output _12,
  output _13,
  output _14,
  output _15
);

  wire not_1_out, not_2_out, not_3_out, not_4_out;

  not not_1 (not_1_out, \input [3]);
  not not_2 (not_2_out, \input [2]);
  not not_3 (not_3_out, \input [1]);
  not not_4 (not_4_out, \input [0]);
  and and_1 (_0, not_1_out, not_2_out, 1'b1, not_3_out, not_4_out);
  and and_2 (_1, not_1_out, not_2_out, 1'b1, not_3_out, \input [0]);
  and and_3 (_2, not_1_out, not_2_out, 1'b1, \input [1], not_4_out);
  and and_4 (_3, not_1_out, not_2_out, 1'b1, \input [1], \input [0]);
  and and_5 (_4, not_1_out, \input [2], not_3_out, not_4_out);
  and and_6 (_5, not_1_out, \input [2], 1'b1, not_3_out, \input [0]);
  and and_7 (_6, not_1_out, \input [2], 1'b1, \input [1], not_4_out);
  and and_8 (_7, not_1_out, \input [2], 1'b1, \input [1], \input [0]);
  and and_9 (_8, \input [3], not_2_out, 1'b1, not_3_out, not_4_out);
  and and_10 (_9, \input [3], not_2_out, 1'b1, not_3_out, \input [0]);
  and and_11 (_10, \input [3], not_2_out, 1'b1, \input [1], not_4_out);
  and and_12 (_11, \input [3], not_2_out, 1'b1, \input [1], \input [0]);
  and and_13 (_12, \input [3], \input [2], 1'b1, not_3_out, not_4_out);
  and and_14 (_13, \input [3], \input [2], 1'b1, not_3_out, \input [0]);
  and and_15 (_14, \input [3], \input [2], 1'b1, \input [1], not_4_out);
  and and_16 (_15, \input [3], \input [2], 1'b1, \input [1], \input [0]);

  // Notes on the sheet:
  //   16 BIT DECODER
  //   this is left for enable bit
endmodule

module Register20 (
  input  [19:0] \input ,
  input  clock,
  input  clear,
  input  enable,
  output [19:0] \output 
);

  D_Flip_Flop d_ff_1 (.clk(clock), .D(\input [19]), .Q(\output [19]), .en(enable), .reset(clear));  // open: Qn, preset
  D_Flip_Flop d_ff_2 (.clk(clock), .D(\input [18]), .Q(\output [18]), .en(enable), .reset(clear));  // open: Qn, preset
  D_Flip_Flop d_ff_3 (.clk(clock), .D(\input [17]), .Q(\output [17]), .en(enable), .reset(clear));  // open: Qn, preset
  D_Flip_Flop d_ff_4 (.clk(clock), .D(\input [16]), .Q(\output [16]), .en(enable), .reset(clear));  // open: Qn, preset
  D_Flip_Flop d_ff_5 (.clk(clock), .D(\input [15]), .Q(\output [15]), .en(enable), .reset(clear));  // open: Qn, preset
  D_Flip_Flop d_ff_6 (.clk(clock), .D(\input [14]), .Q(\output [14]), .en(enable), .reset(clear));  // open: Qn, preset
  D_Flip_Flop d_ff_7 (.clk(clock), .D(\input [13]), .Q(\output [13]), .en(enable), .reset(clear));  // open: Qn, preset
  D_Flip_Flop d_ff_8 (.clk(clock), .D(\input [12]), .Q(\output [12]), .en(enable), .reset(clear));  // open: Qn, preset
  D_Flip_Flop d_ff_9 (.clk(clock), .D(\input [11]), .Q(\output [11]), .en(enable), .reset(clear));  // open: Qn, preset
  D_Flip_Flop d_ff_10 (.clk(clock), .D(\input [10]), .Q(\output [10]), .en(enable), .reset(clear));  // open: Qn, preset
  D_Flip_Flop d_ff_11 (.clk(clock), .D(\input [9]), .Q(\output [9]), .en(enable), .reset(clear));  // open: Qn, preset
  D_Flip_Flop d_ff_12 (.clk(clock), .D(\input [8]), .Q(\output [8]), .en(enable), .reset(clear));  // open: Qn, preset
  D_Flip_Flop d_ff_13 (.clk(clock), .D(\input [7]), .Q(\output [7]), .en(enable), .reset(clear));  // open: Qn, preset
  D_Flip_Flop d_ff_14 (.clk(clock), .D(\input [6]), .Q(\output [6]), .en(enable), .reset(clear));  // open: Qn, preset
  D_Flip_Flop d_ff_15 (.clk(clock), .D(\input [5]), .Q(\output [5]), .en(enable), .reset(clear));  // open: Qn, preset
  D_Flip_Flop d_ff_16 (.clk(clock), .D(\input [4]), .Q(\output [4]), .en(enable), .reset(clear));  // open: Qn, preset
  D_Flip_Flop d_ff_17 (.clk(clock), .D(\input [3]), .Q(\output [3]), .en(enable), .reset(clear));  // open: Qn, preset
  D_Flip_Flop d_ff_18 (.clk(clock), .D(\input [2]), .Q(\output [2]), .en(enable), .reset(clear));  // open: Qn, preset
  D_Flip_Flop d_ff_19 (.clk(clock), .D(\input [1]), .Q(\output [1]), .en(enable), .reset(clear));  // open: Qn, preset
  D_Flip_Flop d_ff_20 (.clk(clock), .D(\input [0]), .Q(\output [0]), .en(enable), .reset(clear));  // open: Qn, preset

  // Notes on the sheet:
  //   20 BIT DECODER
endmodule

module ALU (
  input  [19:0] i0,
  input  [19:0] i1,
  input  enable,
  input  [3:0] opcode_ALU_control,
  output [19:0] \output 
);

  wire [19:0] adder20_1_sum, nand_1_out, or_1_out, sll_1_out_3, sub_1_sum;

  Adder20 adder20_1 (.num0(i0), .num1(i1), .sum(adder20_1_sum));
  assign or_1_out = i0 | i1;  // OR_Gate or_1, 20 bits wide
  assign nand_1_out = ~(i0 & i1);  // NAND_Gate nand_1, 20 bits wide
  sub sub_1 (.sum(sub_1_sum), .num0(i0), .num1(i1));
  Sll sll_1 (.in_1(i0), .in_2(i1), .out_3(sll_1_out_3));
  Multiplexer #(.select(3), .width(20)) multiplexer_1 (
    .in1(adder20_1_sum), .in2(or_1_out), .in3(nand_1_out), .in4(sub_1_sum), .in5(sll_1_out_3),
    .out(\output ), .sel(opcode_ALU_control[2:0]), .en(enable));  // open: in0, in6, in7

  // Notes on the sheet:
  //   number to be shifted
  //   shift amount
  //   unsigned
  //   ALU
  //   add, or, nand, sub, sll, addi, orıi, nandı, subi, slli
endmodule

module DLatch (
  input  D,
  input  clk,
  output Q_prime,
  output Q
);

  wire and_1_out, and_2_out, not_1_out;

  not not_1 (not_1_out, D);
  and and_1 (and_1_out, D, clk);
  and and_2 (and_2_out, not_1_out, clk);
  nor nor_1 (Q_prime, and_1_out, Q);
  nor nor_2 (Q, Q_prime, and_2_out);

  // Notes on the sheet:
  //   D-LATCH
endmodule

module PC (
  input  [11:0] \input ,
  input  JUMP,
  input  clock,
  output [11:0] \output 
);

  wire [11:0] adder12_1_sum, multiplexer_1_out;

  Multiplexer #(.width(12)) multiplexer_1 (.in0(12'h1), .in1(\input ), .out(multiplexer_1_out), .sel(JUMP), .en(1'b1));
  Adder12 adder12_1 (.sum(adder12_1_sum), .num0(\output ), .num1(multiplexer_1_out));
  Register12 register12_1 (.\input (adder12_1_sum), .clock(clock), .clear(1'b0), .enable(1'b1), .\output (\output ));

  // Notes on the sheet:
  //   PROGRAM COUNTER
endmodule

module sub (
  input  [19:0] num0,
  input  [19:0] num1,
  output [19:0] sum
);

  wire fulladder_2_cout, fulladder_3_cout, fulladder_4_cout, fulladder_5_cout, fulladder_6_cout,
       fulladder_7_cout, fulladder_8_cout, fulladder_9_cout, fulladder_10_cout, fulladder_11_cout,
       fulladder_12_cout, fulladder_13_cout, fulladder_14_cout, fulladder_15_cout, fulladder_16_cout,
       fulladder_17_cout, fulladder_18_cout, fulladder_19_cout, fulladder_20_cout;
  wire [19:0] not_1_out;

  assign not_1_out = ~num1;  // NOT_Gate not_1, 20 bits wide
  FullAdder fulladder_1 (.i0(num0[19]), .i1(not_1_out[19]), .cin(fulladder_2_cout), .sum(sum[19]));  // open: cout
  FullAdder fulladder_2 (
    .i0(num0[18]), .i1(not_1_out[18]), .cin(fulladder_3_cout), .sum(sum[18]), .cout(fulladder_2_cout));
  FullAdder fulladder_3 (
    .i0(num0[17]), .i1(not_1_out[17]), .cin(fulladder_4_cout), .sum(sum[17]), .cout(fulladder_3_cout));
  FullAdder fulladder_4 (
    .i0(num0[16]), .i1(not_1_out[16]), .cin(fulladder_5_cout), .sum(sum[16]), .cout(fulladder_4_cout));
  FullAdder fulladder_5 (
    .i0(num0[15]), .i1(not_1_out[15]), .cin(fulladder_6_cout), .sum(sum[15]), .cout(fulladder_5_cout));
  FullAdder fulladder_6 (
    .i0(num0[14]), .i1(not_1_out[14]), .cin(fulladder_7_cout), .sum(sum[14]), .cout(fulladder_6_cout));
  FullAdder fulladder_7 (
    .i0(num0[13]), .i1(not_1_out[13]), .cin(fulladder_8_cout), .sum(sum[13]), .cout(fulladder_7_cout));
  FullAdder fulladder_8 (
    .i0(num0[12]), .i1(not_1_out[12]), .cin(fulladder_9_cout), .sum(sum[12]), .cout(fulladder_8_cout));
  FullAdder fulladder_9 (
    .i0(num0[11]), .i1(not_1_out[11]), .cin(fulladder_10_cout), .sum(sum[11]), .cout(fulladder_9_cout));
  FullAdder fulladder_10 (
    .i0(num0[10]), .i1(not_1_out[10]), .cin(fulladder_11_cout), .sum(sum[10]), .cout(fulladder_10_cout));
  FullAdder fulladder_11 (
    .i0(num0[9]), .i1(not_1_out[9]), .cin(fulladder_12_cout), .sum(sum[9]), .cout(fulladder_11_cout));
  FullAdder fulladder_12 (
    .i0(num0[8]), .i1(not_1_out[8]), .cin(fulladder_13_cout), .sum(sum[8]), .cout(fulladder_12_cout));
  FullAdder fulladder_13 (
    .i0(num0[7]), .i1(not_1_out[7]), .cin(fulladder_14_cout), .sum(sum[7]), .cout(fulladder_13_cout));
  FullAdder fulladder_14 (
    .i0(num0[6]), .i1(not_1_out[6]), .cin(fulladder_15_cout), .sum(sum[6]), .cout(fulladder_14_cout));
  FullAdder fulladder_15 (
    .i0(num0[5]), .i1(not_1_out[5]), .cin(fulladder_16_cout), .sum(sum[5]), .cout(fulladder_15_cout));
  FullAdder fulladder_16 (
    .i0(num0[4]), .i1(not_1_out[4]), .cin(fulladder_18_cout), .sum(sum[4]), .cout(fulladder_16_cout));
  FullAdder fulladder_17 (
    .i0(num0[2]), .i1(not_1_out[2]), .cin(fulladder_19_cout), .sum(sum[2]), .cout(fulladder_17_cout));
  FullAdder fulladder_18 (
    .i0(num0[3]), .i1(not_1_out[3]), .cin(fulladder_17_cout), .sum(sum[3]), .cout(fulladder_18_cout));
  FullAdder fulladder_19 (
    .i0(num0[1]), .i1(not_1_out[1]), .cin(fulladder_20_cout), .sum(sum[1]), .cout(fulladder_19_cout));
  FullAdder fulladder_20 (.i0(num0[0]), .i1(not_1_out[0]), .cin(1'b1), .sum(sum[0]), .cout(fulladder_20_cout));

  // Notes on the sheet:
  //   input0 - input1
  //   SUBSTRACTOR
endmodule

module shiftRegister (
  input  [19:0] \input ,
  input  in_2,
  input  clock,
  input  clear,
  input  enable,
  output [19:0] \output 
);

  wire multiplexer_1_out, multiplexer_2_out, multiplexer_3_out, multiplexer_4_out, multiplexer_5_out,
       multiplexer_6_out, multiplexer_7_out, multiplexer_8_out, multiplexer_9_out, multiplexer_10_out,
       multiplexer_11_out, multiplexer_12_out, multiplexer_13_out, multiplexer_14_out, multiplexer_15_out,
       multiplexer_16_out, multiplexer_17_out, multiplexer_18_out, multiplexer_19_out, multiplexer_20_out,
       or_1_out, undriven, undriven_2;

  Multiplexer multiplexer_1 (.in0(\input [19]), .in1(\output [18]), .out(multiplexer_1_out), .sel(undriven), .en(1'b0));
  Multiplexer multiplexer_2 (.in0(\input [18]), .in1(\output [17]), .out(multiplexer_2_out), .en(1'b0));  // open: sel
  D_Flip_Flop d_ff_1 (
    .clk(clock), .D(multiplexer_1_out), .Q(\output [19]), .en(enable), .reset(clear));  // open: Qn, preset
  Multiplexer multiplexer_3 (
    .in0(\input [17]), .in1(\output [16]), .out(multiplexer_3_out), .sel(undriven_2), .en(1'b0));
  D_Flip_Flop d_ff_2 (
    .clk(clock), .D(multiplexer_2_out), .Q(\output [18]), .en(enable), .reset(clear));  // open: Qn, preset
  Multiplexer multiplexer_4 (.in0(\input [16]), .in1(\output [15]), .out(multiplexer_4_out), .en(1'b0));  // open: sel
  D_Flip_Flop d_ff_3 (
    .clk(clock), .D(multiplexer_3_out), .Q(\output [17]), .en(enable), .reset(clear));  // open: Qn, preset
  Multiplexer multiplexer_5 (.in0(\input [15]), .in1(\output [14]), .out(multiplexer_5_out), .en(1'b0));  // open: sel
  D_Flip_Flop d_ff_4 (
    .clk(clock), .D(multiplexer_4_out), .Q(\output [16]), .en(enable), .reset(clear));  // open: Qn, preset
  D_Flip_Flop d_ff_5 (
    .clk(clock), .D(multiplexer_5_out), .Q(\output [15]), .en(enable), .reset(clear));  // open: Qn, preset
  Multiplexer multiplexer_6 (.in0(\input [14]), .in1(\output [13]), .out(multiplexer_6_out), .en(1'b0));  // open: sel
  D_Flip_Flop d_ff_6 (
    .clk(clock), .D(multiplexer_6_out), .Q(\output [14]), .en(enable), .reset(clear));  // open: Qn, preset
  Multiplexer multiplexer_7 (.in0(\input [13]), .in1(\output [12]), .out(multiplexer_7_out), .en(1'b0));  // open: sel
  D_Flip_Flop d_ff_7 (
    .clk(clock), .D(multiplexer_7_out), .Q(\output [13]), .en(enable), .reset(clear));  // open: Qn, preset
  Multiplexer multiplexer_8 (.in0(\input [12]), .in1(\output [11]), .out(multiplexer_8_out), .en(1'b0));  // open: sel
  Multiplexer multiplexer_9 (.in0(\input [11]), .in1(\output [10]), .out(multiplexer_9_out), .en(1'b0));  // open: sel
  D_Flip_Flop d_ff_8 (
    .clk(clock), .D(multiplexer_8_out), .Q(\output [12]), .en(enable), .reset(clear));  // open: Qn, preset
  Multiplexer multiplexer_10 (.in0(\input [10]), .in1(\output [9]), .out(multiplexer_10_out), .en(1'b0));  // open: sel
  D_Flip_Flop d_ff_9 (
    .clk(clock), .D(multiplexer_9_out), .Q(\output [11]), .en(enable), .reset(clear));  // open: Qn, preset
  Multiplexer multiplexer_11 (.in0(\input [9]), .in1(\output [8]), .out(multiplexer_11_out), .en(1'b0));  // open: sel
  D_Flip_Flop d_ff_10 (
    .clk(clock), .D(multiplexer_10_out), .Q(\output [10]), .en(enable), .reset(clear));  // open: Qn, preset
  Multiplexer multiplexer_12 (.in0(\input [8]), .in1(\output [7]), .out(multiplexer_12_out), .en(1'b0));  // open: sel
  D_Flip_Flop d_ff_11 (
    .clk(clock), .D(multiplexer_11_out), .Q(\output [9]), .en(enable), .reset(clear));  // open: Qn, preset
  Multiplexer multiplexer_13 (.in0(\input [7]), .in1(\output [6]), .out(multiplexer_13_out), .en(1'b0));  // open: sel
  D_Flip_Flop d_ff_12 (
    .clk(clock), .D(multiplexer_12_out), .Q(\output [8]), .en(enable), .reset(clear));  // open: Qn, preset
  D_Flip_Flop d_ff_13 (
    .clk(clock), .D(multiplexer_13_out), .Q(\output [7]), .en(enable), .reset(clear));  // open: Qn, preset
  Multiplexer multiplexer_14 (.in0(\input [6]), .in1(\output [5]), .out(multiplexer_14_out), .en(1'b0));  // open: sel
  D_Flip_Flop d_ff_14 (
    .clk(clock), .D(multiplexer_14_out), .Q(\output [6]), .en(enable), .reset(clear));  // open: Qn, preset
  Multiplexer multiplexer_15 (.in0(\input [5]), .in1(\output [4]), .out(multiplexer_15_out), .en(1'b0));  // open: sel
  D_Flip_Flop d_ff_15 (
    .clk(clock), .D(multiplexer_15_out), .Q(\output [5]), .en(enable), .reset(clear));  // open: Qn, preset
  Multiplexer multiplexer_16 (.in0(\input [4]), .in1(\output [3]), .out(multiplexer_16_out), .en(1'b0));  // open: sel
  Multiplexer multiplexer_17 (.in0(\input [3]), .in1(\output [2]), .out(multiplexer_17_out), .en(1'b0));  // open: sel
  D_Flip_Flop d_ff_16 (
    .clk(clock), .D(multiplexer_16_out), .Q(\output [4]), .en(enable), .reset(clear));  // open: Qn, preset
  Multiplexer multiplexer_18 (.in0(\input [2]), .in1(\output [1]), .out(multiplexer_18_out), .en(1'b0));  // open: sel
  D_Flip_Flop d_ff_17 (
    .clk(clock), .D(multiplexer_17_out), .Q(\output [3]), .en(enable), .reset(clear));  // open: Qn, preset
  Multiplexer multiplexer_19 (.in0(\input [1]), .in1(\output [0]), .out(multiplexer_19_out), .en(1'b0));  // open: sel
  D_Flip_Flop d_ff_18 (
    .clk(clock), .D(multiplexer_18_out), .Q(\output [2]), .en(enable), .reset(clear));  // open: Qn, preset
  Multiplexer multiplexer_20 (.in0(\input [0]), .in1(in_2), .out(multiplexer_20_out), .en(1'b0));  // open: sel
  D_Flip_Flop d_ff_19 (
    .clk(clock), .D(multiplexer_19_out), .Q(\output [1]), .en(enable), .reset(clear));  // open: Qn, preset
  D_Flip_Flop d_ff_20 (
    .clk(clock), .D(multiplexer_20_out), .Q(\output [0]), .en(enable), .reset(clear));  // open: Qn, preset
  buf or_1 (or_1_out, clear);  // OR_Gate
endmodule

module Sll (
  input  [19:0] in_1,
  input  [19:0] in_2,
  output [19:0] out_3
);

  wire [4:0] multiplexer_1_out;
  wire [4:4] or_1_out;

  or or_1 (or_1_out[4], in_2[5], in_2[6], in_2[7], in_2[8], in_2[9], in_2[10], in_2[11], in_2[12], in_2[13], in_2[14], in_2[15], in_2[16], in_2[17], in_2[18], in_2[19]);
  Multiplexer #(.width(5)) multiplexer_1 (
    .in0(in_2[4:0]), .in1({5{or_1_out[4]}}), .out(multiplexer_1_out), .sel(or_1_out[4]), .en(1'b1));
  Multiplexer #(.select(5), .width(20)) multiplexer_2 (
    .in0(in_1), .in1({in_1[18:0], 1'b0}), .in2({in_1[17:0], 2'b00}), .in3({in_1[16:0], 3'b000}),
    .in4({in_1[15:0], 4'b0000}), .in5({in_1[14:0], {5{1'b0}}}), .in6({in_1[13:0], {6{1'b0}}}),
    .in7({in_1[12:0], {7{1'b0}}}), .in8({in_1[11:0], {8{1'b0}}}), .in9({in_1[10:0], {9{1'b0}}}),
    .in10({in_1[9:0], {10{1'b0}}}), .in11({in_1[8:0], {11{1'b0}}}), .in12({in_1[7:0], {12{1'b0}}}),
    .in13({in_1[6:0], {13{1'b0}}}), .in14({in_1[5:0], {14{1'b0}}}), .in15({in_1[4:0], {15{1'b0}}}),
    .in16({in_1[3:0], {16{1'b0}}}), .in17({in_1[2:0], {17{1'b0}}}), .in18({in_1[1:0], {18{1'b0}}}),
    .in19({in_1[0], {19{1'b0}}}), .in20({20{1'b0}}), .in21({20{1'b0}}), .in22({20{1'b0}}), .in23({20{1'b0}}),
    .in24({20{1'b0}}), .in25({20{1'b0}}), .in26({20{1'b0}}), .in27({20{1'b0}}), .in28({20{1'b0}}),
    .in29({20{1'b0}}), .in30({20{1'b0}}), .in31({20{1'b0}}), .out(out_3), .sel(multiplexer_1_out), .en(1'b1));

  // Notes on the sheet:
  //   SHIFT LOGICALLY LEFT
endmodule

module Register12 (
  input  [11:0] \input ,
  input  clock,
  input  clear,
  input  enable,
  output [11:0] \output 
);

  D_Flip_Flop d_ff_1 (.clk(clock), .D(\input [11]), .Q(\output [11]), .en(enable), .reset(clear));  // open: Qn, preset
  D_Flip_Flop d_ff_2 (.clk(clock), .D(\input [10]), .Q(\output [10]), .en(enable), .reset(clear));  // open: Qn, preset
  D_Flip_Flop d_ff_3 (.clk(clock), .D(\input [9]), .Q(\output [9]), .en(enable), .reset(clear));  // open: Qn, preset
  D_Flip_Flop d_ff_4 (.clk(clock), .D(\input [8]), .Q(\output [8]), .en(enable), .reset(clear));  // open: Qn, preset
  D_Flip_Flop d_ff_5 (.clk(clock), .D(\input [7]), .Q(\output [7]), .en(enable), .reset(clear));  // open: Qn, preset
  D_Flip_Flop d_ff_6 (.clk(clock), .D(\input [6]), .Q(\output [6]), .en(enable), .reset(clear));  // open: Qn, preset
  D_Flip_Flop d_ff_7 (.clk(clock), .D(\input [5]), .Q(\output [5]), .en(enable), .reset(clear));  // open: Qn, preset
  D_Flip_Flop d_ff_8 (.clk(clock), .D(\input [4]), .Q(\output [4]), .en(enable), .reset(clear));  // open: Qn, preset
  D_Flip_Flop d_ff_9 (.clk(clock), .D(\input [3]), .Q(\output [3]), .en(enable), .reset(clear));  // open: Qn, preset
  D_Flip_Flop d_ff_10 (.clk(clock), .D(\input [2]), .Q(\output [2]), .en(enable), .reset(clear));  // open: Qn, preset
  D_Flip_Flop d_ff_11 (.clk(clock), .D(\input [1]), .Q(\output [1]), .en(enable), .reset(clear));  // open: Qn, preset
  D_Flip_Flop d_ff_12 (.clk(clock), .D(\input [0]), .Q(\output [0]), .en(enable), .reset(clear));  // open: Qn, preset

  // Notes on the sheet:
  //   12 BITS REGISTER
endmodule

module SignExtender7to20 (
  input  [19:0] In,
  output [19:0] OUT
);

  Multiplexer #(.width(14)) multiplexer_1 (.in0({14{1'b0}}), .in1({14{1'b1}}), .out(OUT[19:6]), .sel(In[6]), .en(1'b1));

  assign OUT[5:0] = In[5:0];

  // Notes on the sheet:
  //   SIGN EXTENDER 7 TO 20
endmodule

module ZeroExtender12to16 (
  input  [11:0] in_1,
  output [15:0] out_2
);


  assign out_2 = {4'b0000, in_1};

  // Notes on the sheet:
  //   SIGN EXTENDER 12 TO 16
  //   16 BIT DECODER
endmodule

module ZeroExtender5to16 (
  input  [4:0] in_1,
  output [15:0] out_2
);


  assign out_2 = {{11{1'b0}}, in_1};

  // Notes on the sheet:
  //   SIGN EXTENDER 5 TO 16
endmodule

module HalfCompare (
  input  A,
  input  B,
  output lt,
  output Gt,
  output Eq
);

  wire not_1_out, not_2_out;

  not not_1 (not_1_out, A);
  not not_2 (not_2_out, B);
  and and_1 (lt, not_1_out, B);
  and and_2 (Gt, A, not_2_out);
  xnor xnor_1 (Eq, A, B);

  // Notes on the sheet:
  //   HALF COMPERATOR
endmodule

module FullCompare (
  input  A,
  input  B,
  input  LtIn,
  input  GtIn,
  input  EqIn,
  output Lt,
  output Gt,
  output Eq
);

  wire and_1_out, and_2_out, not_1_out, not_2_out, xnor_1_out;

  not not_1 (not_1_out, A);
  not not_2 (not_2_out, B);
  xnor xnor_1 (xnor_1_out, A, B);
  and and_1 (and_1_out, not_1_out, EqIn, B);
  and and_2 (and_2_out, A, EqIn, not_2_out);
  and and_3 (Eq, xnor_1_out, EqIn);
  or or_1 (Lt, and_1_out, LtIn);
  or or_2 (Gt, GtIn, and_2_out);

  // Notes on the sheet:
  //   FULL COMPERATOR
endmodule

module Controller (
  input  [19:0] \input ,
  input  [2:0] BCMP_bits,
  output [3:0] src2,
  output Mux1_imm_or_register,
  output [3:0] src1_op2,
  output ALU_enable_if_it_is_an_arithmetic_operation,
  output [3:0] dest_op1_srcST,
  output WriteEnable_ALU_MEM,
  output rd2_select_registerfile,
  output load_MemRead,
  output store_MemWrite,
  output wr_select_registerfile,
  output InstructionRead,
  output BCMP_ENABLE,
  output PCRead,
  output JUMP,
  output JUMP_MUX_SELECT
);

  wire decoder_1_out1, decoder_1_out2, decoder_1_out3, decoder_1_out4, decoder_1_out5, decoder_1_out9,
       decoder_1_out10, decoder_1_out11, decoder_1_out12, decoder_1_out14, JUMP_BCMP, or_2_out;
  wire [2:0] and_1_out;

  assign and_1_out = \input [18:16] & BCMP_bits;  // AND_Gate and_1, 3 bits wide
  or or_1 (JUMP, JUMP_BCMP, JUMP_MUX_SELECT);
  Decoder #(.select(4), .enable("false")) decoder_1 (
    .out1(decoder_1_out1), .out2(decoder_1_out2), .out3(decoder_1_out3), .out4(decoder_1_out4),
    .out5(decoder_1_out5), .out6(load_MemRead), .out7(store_MemWrite), .out8(JUMP_MUX_SELECT),
    .out9(decoder_1_out9), .out10(decoder_1_out10), .out11(decoder_1_out11), .out12(decoder_1_out12),
    .out14(decoder_1_out14), .sel(\input [19:16]));  // open: out0, out13, out15
  or or_2 (or_2_out, and_1_out[0], and_1_out[1], and_1_out[2]);
  and and_2 (JUMP_BCMP, or_2_out, BCMP_ENABLE);
  or or_3 (ALU_enable_if_it_is_an_arithmetic_operation, decoder_1_out1, decoder_1_out2, decoder_1_out3, decoder_1_out4, decoder_1_out5);
  or or_4 (BCMP_ENABLE, decoder_1_out9, decoder_1_out10, decoder_1_out11, decoder_1_out12, decoder_1_out14);
  or or_5 (WriteEnable_ALU_MEM, ALU_enable_if_it_is_an_arithmetic_operation, load_MemRead);

  assign dest_op1_srcST = \input [15:12];
  assign InstructionRead = 1'b1;
  assign Mux1_imm_or_register = \input [7];
  assign PCRead = 1'b1;
  assign rd2_select_registerfile = load_MemRead;
  assign src1_op2 = \input [11:8];
  assign src2 = \input [3:0];
  assign wr_select_registerfile = store_MemWrite;

  // Other names for the same wires on the sheet: IMM_JUMP = JUMP_MUX_SELECT

  // Notes on the sheet:
  //   Ld 6
  //   str 7
  //   jump 8
  //   TODO CHECK LOGİC
  //   Controller
endmodule

module ZeroExtender12To20 (
  input  [11:0] input_12,
  output [19:0] output_20
);


  assign output_20 = {{8{1'b0}}, input_12};

  // Notes on the sheet:
  //   ZERO EXTENDER 12 TO 20
  //   16 BIT DECODER
endmodule

module Adder12 (
  input  [11:0] num0,
  input  [11:0] num1,
  output [11:0] sum
);

  wire fulladder_2_cout, fulladder_3_cout, fulladder_4_cout, fulladder_5_cout, fulladder_6_cout,
       fulladder_7_cout, fulladder_8_cout, fulladder_9_cout, fulladder_10_cout, fulladder_11_cout,
       fulladder_12_cout;

  FullAdder fulladder_1 (.i0(num0[11]), .i1(num1[11]), .cin(fulladder_2_cout), .sum(sum[11]));  // open: cout
  FullAdder fulladder_2 (.i0(num0[10]), .i1(num1[10]), .cin(fulladder_3_cout), .sum(sum[10]), .cout(fulladder_2_cout));
  FullAdder fulladder_3 (.i0(num0[9]), .i1(num1[9]), .cin(fulladder_4_cout), .sum(sum[9]), .cout(fulladder_3_cout));
  FullAdder fulladder_4 (.i0(num0[8]), .i1(num1[8]), .cin(fulladder_5_cout), .sum(sum[8]), .cout(fulladder_4_cout));
  FullAdder fulladder_5 (.i0(num0[7]), .i1(num1[7]), .cin(fulladder_6_cout), .sum(sum[7]), .cout(fulladder_5_cout));
  FullAdder fulladder_6 (.i0(num0[6]), .i1(num1[6]), .cin(fulladder_8_cout), .sum(sum[6]), .cout(fulladder_6_cout));
  FullAdder fulladder_7 (.i0(num0[4]), .i1(num1[4]), .cin(fulladder_9_cout), .sum(sum[4]), .cout(fulladder_7_cout));
  FullAdder fulladder_8 (.i0(num0[5]), .i1(num1[5]), .cin(fulladder_7_cout), .sum(sum[5]), .cout(fulladder_8_cout));
  FullAdder fulladder_9 (.i0(num0[3]), .i1(num1[3]), .cin(fulladder_10_cout), .sum(sum[3]), .cout(fulladder_9_cout));
  FullAdder fulladder_10 (.i0(num0[2]), .i1(num1[2]), .cin(fulladder_11_cout), .sum(sum[2]), .cout(fulladder_10_cout));
  FullAdder fulladder_11 (.i0(num0[1]), .i1(num1[1]), .cin(fulladder_12_cout), .sum(sum[1]), .cout(fulladder_11_cout));
  FullAdder fulladder_12 (.i0(num0[0]), .i1(num1[0]), .cin(1'b0), .sum(sum[0]), .cout(fulladder_12_cout));

  // Notes on the sheet:
  //   12 BIT ADDER
endmodule

module SignExtender8to12 (
  input  [7:0] In,
  output [11:0] OUT
);

  Multiplexer #(.width(5)) multiplexer_1 (.in0({5{1'b0}}), .in1({5{1'b1}}), .out(OUT[11:7]), .sel(In[7]), .en(1'b1));

  assign OUT[6:0] = In[6:0];
endmodule

module Compare20 (
  input  [19:0] A,
  input  [19:0] B,
  output [2:0] out_3
);

  wire fullcompare_1_eq, fullcompare_1_gt, fullcompare_1_lt, fullcompare_2_eq, fullcompare_2_gt,
       fullcompare_2_lt, fullcompare_3_eq, fullcompare_3_gt, fullcompare_3_lt, fullcompare_4_eq,
       fullcompare_4_gt, fullcompare_4_lt, fullcompare_5_eq, fullcompare_5_gt, fullcompare_5_lt,
       fullcompare_6_eq, fullcompare_6_gt, fullcompare_6_lt, fullcompare_7_eq, fullcompare_7_gt,
       fullcompare_7_lt, fullcompare_8_eq, fullcompare_8_gt, fullcompare_8_lt, fullcompare_9_eq,
       fullcompare_9_gt, fullcompare_9_lt, fullcompare_10_eq, fullcompare_10_gt, fullcompare_10_lt,
       fullcompare_11_eq, fullcompare_11_gt, fullcompare_11_lt, fullcompare_12_eq, fullcompare_12_gt,
       fullcompare_12_lt, fullcompare_13_eq, fullcompare_13_gt, fullcompare_13_lt, fullcompare_14_eq,
       fullcompare_14_gt, fullcompare_14_lt, fullcompare_15_eq, fullcompare_15_gt, fullcompare_15_lt,
       fullcompare_16_eq, fullcompare_16_gt, fullcompare_16_lt, fullcompare_17_eq, fullcompare_17_gt,
       fullcompare_17_lt, fullcompare_18_eq, fullcompare_18_gt, fullcompare_18_lt, fullcompare_20_eq,
       fullcompare_20_gt, fullcompare_20_lt;

  FullCompare fullcompare_1 (
    .A(A[19]), .B(B[19]), .LtIn(1'b0), .GtIn(1'b0), .EqIn(1'b1), .Lt(fullcompare_1_lt),
    .Gt(fullcompare_1_gt), .Eq(fullcompare_1_eq));
  FullCompare fullcompare_2 (
    .A(A[18]), .B(B[18]), .LtIn(fullcompare_1_lt), .GtIn(fullcompare_1_gt), .EqIn(fullcompare_1_eq),
    .Lt(fullcompare_2_lt), .Gt(fullcompare_2_gt), .Eq(fullcompare_2_eq));
  FullCompare fullcompare_3 (
    .A(A[17]), .B(B[17]), .LtIn(fullcompare_2_lt), .GtIn(fullcompare_2_gt), .EqIn(fullcompare_2_eq),
    .Lt(fullcompare_3_lt), .Gt(fullcompare_3_gt), .Eq(fullcompare_3_eq));
  FullCompare fullcompare_4 (
    .A(A[16]), .B(B[16]), .LtIn(fullcompare_3_lt), .GtIn(fullcompare_3_gt), .EqIn(fullcompare_3_eq),
    .Lt(fullcompare_4_lt), .Gt(fullcompare_4_gt), .Eq(fullcompare_4_eq));
  FullCompare fullcompare_5 (
    .A(A[14]), .B(B[14]), .LtIn(fullcompare_6_lt), .GtIn(fullcompare_6_gt), .EqIn(fullcompare_6_eq),
    .Lt(fullcompare_5_lt), .Gt(fullcompare_5_gt), .Eq(fullcompare_5_eq));
  FullCompare fullcompare_6 (
    .A(A[15]), .B(B[15]), .LtIn(fullcompare_4_lt), .GtIn(fullcompare_4_gt), .EqIn(fullcompare_4_eq),
    .Lt(fullcompare_6_lt), .Gt(fullcompare_6_gt), .Eq(fullcompare_6_eq));
  FullCompare fullcompare_7 (
    .A(A[13]), .B(B[13]), .LtIn(fullcompare_5_lt), .GtIn(fullcompare_5_gt), .EqIn(fullcompare_5_eq),
    .Lt(fullcompare_7_lt), .Gt(fullcompare_7_gt), .Eq(fullcompare_7_eq));
  FullCompare fullcompare_8 (
    .A(A[12]), .B(B[12]), .LtIn(fullcompare_7_lt), .GtIn(fullcompare_7_gt), .EqIn(fullcompare_7_eq),
    .Lt(fullcompare_8_lt), .Gt(fullcompare_8_gt), .Eq(fullcompare_8_eq));
  FullCompare fullcompare_9 (
    .A(A[10]), .B(B[10]), .LtIn(fullcompare_10_lt), .GtIn(fullcompare_10_gt), .EqIn(fullcompare_10_eq),
    .Lt(fullcompare_9_lt), .Gt(fullcompare_9_gt), .Eq(fullcompare_9_eq));
  FullCompare fullcompare_10 (
    .A(A[11]), .B(B[11]), .LtIn(fullcompare_8_lt), .GtIn(fullcompare_8_gt), .EqIn(fullcompare_8_eq),
    .Lt(fullcompare_10_lt), .Gt(fullcompare_10_gt), .Eq(fullcompare_10_eq));
  FullCompare fullcompare_11 (
    .A(A[9]), .B(B[9]), .LtIn(fullcompare_9_lt), .GtIn(fullcompare_9_gt), .EqIn(fullcompare_9_eq),
    .Lt(fullcompare_11_lt), .Gt(fullcompare_11_gt), .Eq(fullcompare_11_eq));
  FullCompare fullcompare_12 (
    .A(A[8]), .B(B[8]), .LtIn(fullcompare_11_lt), .GtIn(fullcompare_11_gt), .EqIn(fullcompare_11_eq),
    .Lt(fullcompare_12_lt), .Gt(fullcompare_12_gt), .Eq(fullcompare_12_eq));
  FullCompare fullcompare_13 (
    .A(A[6]), .B(B[6]), .LtIn(fullcompare_14_lt), .GtIn(fullcompare_14_gt), .EqIn(fullcompare_14_eq),
    .Lt(fullcompare_13_lt), .Gt(fullcompare_13_gt), .Eq(fullcompare_13_eq));
  FullCompare fullcompare_14 (
    .A(A[7]), .B(B[7]), .LtIn(fullcompare_12_lt), .GtIn(fullcompare_12_gt), .EqIn(fullcompare_12_eq),
    .Lt(fullcompare_14_lt), .Gt(fullcompare_14_gt), .Eq(fullcompare_14_eq));
  FullCompare fullcompare_15 (
    .A(A[4]), .B(B[4]), .LtIn(fullcompare_16_lt), .GtIn(fullcompare_16_gt), .EqIn(fullcompare_16_eq),
    .Lt(fullcompare_15_lt), .Gt(fullcompare_15_gt), .Eq(fullcompare_15_eq));
  FullCompare fullcompare_16 (
    .A(A[5]), .B(B[5]), .LtIn(fullcompare_13_lt), .GtIn(fullcompare_13_gt), .EqIn(fullcompare_13_eq),
    .Lt(fullcompare_16_lt), .Gt(fullcompare_16_gt), .Eq(fullcompare_16_eq));
  FullCompare fullcompare_17 (
    .A(A[3]), .B(B[3]), .LtIn(fullcompare_15_lt), .GtIn(fullcompare_15_gt), .EqIn(fullcompare_15_eq),
    .Lt(fullcompare_17_lt), .Gt(fullcompare_17_gt), .Eq(fullcompare_17_eq));
  FullCompare fullcompare_18 (
    .A(A[2]), .B(B[2]), .LtIn(fullcompare_17_lt), .GtIn(fullcompare_17_gt), .EqIn(fullcompare_17_eq),
    .Lt(fullcompare_18_lt), .Gt(fullcompare_18_gt), .Eq(fullcompare_18_eq));
  FullCompare fullcompare_19 (
    .A(A[0]), .B(B[0]), .LtIn(fullcompare_20_lt), .GtIn(fullcompare_20_gt), .EqIn(fullcompare_20_eq),
    .Lt(out_3[2]), .Gt(out_3[0]), .Eq(out_3[1]));
  FullCompare fullcompare_20 (
    .A(A[1]), .B(B[1]), .LtIn(fullcompare_18_lt), .GtIn(fullcompare_18_gt), .EqIn(fullcompare_18_eq),
    .Lt(fullcompare_20_lt), .Gt(fullcompare_20_gt), .Eq(fullcompare_20_eq));

  // Notes on the sheet:
  //   20 BIT COMPERATOR
endmodule
